# Fritzing sketch microPythonAndIoT (saved by Fritzing 0.9.3b)
breadboards: 3

parts:
  R1 = Resistor [tolerance=±5% resistance=220 package=THT]  # not connected
  C1 = Ceramic Capacitor [capacitance=100nF package="100 mil [THT, multilayer]"]  # not connected
  C2 = Tantalum Capacitor [capacitance=1μF package="100 mil [THT, tantalum]"]  # not connected
  C3 = Electrolytic Capacitor [capacitance=1µF package="100 mil [THT, electrolytic]"]  # not connected
  L1 = Inductor [package="400 mil [THT]"]  # not connected
  D1 = Rectifier Diode [part_number=1N4001 package="300 mil [THT]"]  # not connected
  Q1 = PNP-Transistor [package="TO92 [THT]"]  # not connected
  Q2 = NPN-Transistor [package="TO92 [THT]"]  # not connected
  Q3 = Basic FET P-Channel [package="TO220 [THT]"]  # not connected
  R2 = Trimmer Potentiometer [maximum_resistance=10kΩ package=THT]  # not connected
  R3 = Rotary Potentiometer (Small) [maximum_resistance=100kΩ package=THT]  # not connected
  S1 = Pushbutton [package="[THT]"]  # not connected
  R4 = Photocell (LDR) [package=THT]  # not connected
  RHT1 = Humidity and Temperature Sensor RHT03  # not connected
  Mod1 = Raspberry Pi Pico
  U1 = 2-Channel 5v Relay Shield [package=relay-2ch5v10a]  # not connected
  U2 = lolin
  U3 = ESP32-38PinWide [part_number=ESP32-38PinWide]
  LED1 = LED - 5mm [color="Red (633nm)" package="5 mm [THT]"]  # not connected
  LED2 = LED - 5mm [color="Red (633nm)" package="5 mm [THT]"]  # not connected
  LED3 = LED - 5mm [color="Red (633nm)" package="5 mm [THT]"]
  LED4 = LED - 5mm [color="Red (633nm)" package="5 mm [THT]"]
  LED5 = LED - 5mm [color="Red (633nm)" package="5 mm [THT]"]
  LED6 = LED - 5mm [color="Red (633nm)" package="5 mm [THT]"]
  LED7 = LED - 5mm [color="Red (633nm)" package="5 mm [THT]"]
  R5 = Resistor [tolerance=±5% resistance=220 package=THT]
  R6 = Resistor [tolerance=±5% resistance=220 package=THT]
  R7 = Resistor [tolerance=±5% resistance=220 package=THT]
  R8 = Resistor [tolerance=±5% resistance=220 package=THT]
  R9 = Resistor [tolerance=±5% resistance=220 package=THT]
  DHT1 = DHT22 Humidity and Temperature Sensor  # not connected

nets:
  N1: Mod1.pin_1, U3.GPIO34
  N2: Mod1.pin_2, U3.GPIO39
  N3: Mod1.pin_3, Mod1.pin_8, Mod1.pin_13, Mod1.pin_18, Mod1.pin_23, Mod1.pin_28, Mod1.pin_33, Mod1.pin_38, U3.GPIO36
  N4: Mod1.pin_4, U3.EN
  N5: Mod1.pin_5, U3.3.3
  N6: U2.connector0, R5.Pin_0, R6.Pin_0, R7.Pin_0, R8.Pin_0
  N7: U2.connector15, LED3.cathode, LED4.cathode, LED5.cathode, LED6.cathode, LED7.cathode
  N8: U2.connector33, R9.Pin_0
  N9: LED3.anode, R5.Pin_1
  N10: LED4.anode, R6.Pin_1
  N11: LED5.anode, R7.Pin_1
  N12: LED6.anode, R8.Pin_1
  N13: LED7.anode, R9.Pin_1

custom parts:
  Raspberry Pi Pico: Raspberry Pi Pico. Based around the RP2040 microcontroller the Pico is a low cost microcontroller device bringing Raspberry Pi quality, cost, and easy of use to the microcontroller space. Jan 2021, Split part in to two versions: SMD (this one) and tht. This one is single sided and uses the castellation pads to solder the module to the board (no holes, other than for the USB connector!). The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
  2-Channel 5v Relay Shield: 2 Channel 5v Relay Shield w. 2x SPD-06VDC-SD-C
  ESP32-38PinWide: Generic 38-Pin ESP32 with wide format (only access to one side of pins on a breadboard) based on Stephen Lilley's HiLetgo ESP-WROOM-32 ESP32 ESP-32S Development Board.
