# Fritzing sketch ep11 (saved by Fritzing 0.9.3b)
breadboards: 1

parts:
  U1 = lolin
  DHT1 = DHT22 Humidity and Temperature Sensor
  U2 = 2-Channel 5v Relay Shield [package=relay-2ch5v10a]
  Display1 = LCD screen 16x2 IIC [part_number=101290]

nets:
  N1: U1.connector4, U2.IN1
  N2: U1.connector6, Display1.VCC
  N3: U1.connector7, Display1.SDA
  VDD: U1.connector14, DHT1.VDD, U2.VCC
  N4: U1.connector15, DHT1.NULL, U2.GND, Display1.SCL
  N5: U1.connector25, Display1.GND
  N6: U1.connector33, DHT1.DATA

custom parts:
  2-Channel 5v Relay Shield: 2 Channel 5v Relay Shield w. 2x SPD-06VDC-SD-C
  LCD screen 16x2 IIC: LCD screen with HD44780 controller enables showing text, symbols, value or anything else that comes from Croduino/Arduino. It is capable of showing 16 symbols in two lines and therefore can be used in many projects that need to send clearly visible and legible output information.. • Color of symbols: White • Backlight: Blue • Dimensions: 80 x 36 x 12 mm • Screen dimensions: 64.5 x 16 mm •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
